// Logisim project 4 BIT SYNCHRONOUS.circ as structural Verilog: 1 circuit, main circuit main
module main (
  input  UP_DOWN,
  output out_2,
  output out_3,
  output out_4,
  output out_5
);

  wire and_1_out, and_2_out, and_3_out, and_4_out, and_5_out, and_6_out, clock_out, d_ff_1_qn, d_ff_2_qn,
       d_ff_3_qn, not_1_out, or_1_out, or_2_out, or_3_out, or_4_out, reset_out, xor_1_out, xor_2_out,
       xor_3_out, xor_4_out;

  not not_1 (not_1_out, UP_DOWN);
  and and_1 (and_1_out, not_1_out, d_ff_1_qn);
  and and_2 (and_2_out, and_1_out, d_ff_2_qn);
  and and_3 (and_3_out, and_2_out, d_ff_3_qn);
  and and_4 (and_4_out, UP_DOWN, out_2);
  and and_5 (and_5_out, and_4_out, out_3);
  and and_6 (and_6_out, and_5_out, out_4);
  or or_1 (or_1_out, UP_DOWN, not_1_out);
  or or_2 (or_2_out, and_4_out, and_1_out);
  or or_3 (or_3_out, and_5_out, and_2_out);
  or or_4 (or_4_out, and_6_out, and_3_out);
  xor xor_1 (xor_1_out, out_2, or_1_out);
  xor xor_2 (xor_2_out, out_3, or_2_out);
  xor xor_3 (xor_3_out, out_4, or_3_out);
  xor xor_4 (xor_4_out, out_5, or_4_out);
  Clock clock (.out(clock_out));
  D_Flip_Flop d_ff_1 (
    .clk(clock_out), .D(xor_1_out), .Q(out_2), .Qn(d_ff_1_qn), .reset(reset_out));  // open: preset, en
  D_Flip_Flop d_ff_2 (
    .clk(clock_out), .D(xor_2_out), .Q(out_3), .Qn(d_ff_2_qn), .reset(reset_out));  // open: preset, en
  D_Flip_Flop d_ff_3 (
    .clk(clock_out), .D(xor_3_out), .Q(out_4), .Qn(d_ff_3_qn), .reset(reset_out));  // open: preset, en
  D_Flip_Flop d_ff_4 (.clk(clock_out), .D(xor_4_out), .Q(out_5), .reset(reset_out));  // open: Qn, preset, en
  Button reset (.out(reset_out));
endmodule
